# Fritzing sketch Message Box V1.5 (saved by Fritzing 0.9.4)
circuit board: 5cm x 5cm
circuit board: 4.5cm x 4.5cm
circuit board: 5.4cm x 5.4cm
breadboards: 1

parts:
  IC = NodeMCU V1.0
  OFF/ON = Toggle Switch [package=THT]
  +9V- = Battery block 9V
  100uF = Electrolytic Capacitor [capacitance=100µF package="100 mil [THT, electrolytic]"]
  J1 = female pin header, 15 pins [form="♀ (female)"]
  D7 = Pushbutton [package="[THT]"]
  D6 = Pushbutton [package="[THT]"]
  D5 = Pushbutton [package="[THT]"]
  B1 = Pad [width=4 height=2 connect=center]
  TRIM = Trimmer Potentiometer [maximum_resistance=10kΩ package=THT]
  7905 = Voltage Regulator - 5V [package="TO220 [THT]"]
  10kΩ = Resistor [tolerance=±5% resistance=10k package=THT]
  B2 = Pad [width=4 height=2 connect=center]
  B3 = Pad [width=4 height=2 connect=center]
  LCD = female pin header, 8 pins [form="♀ (female)"]
  - = Pad [width=6 height=4.7 connect=center]
  RST = Pad [width=4 height=2 connect=center]
  CE = Pad [width=4 height=2 connect=center]
  DC = Pad [width=4 height=2 connect=center]
  DIN = Pad [width=4 height=2 connect=center]
  CLK = Pad [width=4 height=2 connect=center]
  A0 = Pad [width=6 height=4.7 connect=center]
  BL = Pad [width=4 height=2 connect=center]
  + = Pad [width=6 height=4.7 connect=center]  # not connected
  POT = Pad [width=4 height=2 connect=center]
  -_2 = Pad [width=4 height=2 connect=center]
  10kΩ_2 = Resistor [tolerance=±5% resistance=10k package=THT]
  10kΩ_3 = Resistor [tolerance=±5% resistance=10k package=THT]
  1kΩ = Resistor [tolerance=±5% resistance=220 package=THT]
  10kΩ_4 = Resistor [tolerance=±5% resistance=330 package=THT]
  10kΩ_5 = Resistor [tolerance=±5% resistance=220 package=THT]
  330Ω = Resistor [tolerance=±5% resistance=330 package=THT]
  A0_2 = female pin header, 2 pins [form="♀ (female)"]
  J2 = female pin header, 15 pins [form="♀ (female)"]
  -_3 = female pin header, 8 pins [form="♀ (female)"]
  5V = female pin header, 8 pins [form="♀ (female)"]
  3_3V = female pin header, 8 pins [form="♀ (female)"]
  D5_2 = female pin header, 3 pins [form="♀ (female)"]
  LED = female pin header, 2 pins [form="♀ (female)"]
  +_2 = Pad [width=4 height=2 connect=center]
  D0 = rounded female pin header, 5 pins [form="♀ (female rounded)"]  # not connected

nets:
  N1: IC.3V3, 100uF.+, 3_3V.pin1, 3_3V.pin2, 3_3V.pin3, 3_3V.pin4, 3_3V.pin5, 3_3V.pin6, 3_3V.pin7, 3_3V.pin8
  N2: IC.GND, +9V-.-, TRIM.leg1, 7905.output_voltage
  N3: IC.Vin, OFF/ON.L1, 7905.input_voltage
  N4: OFF/ON.COM, OFF/ON.L2, +9V-.+
  N5: 100uF.-, J2.pin14, -_3.pin1, -_3.pin2, -_3.pin3, -_3.pin4, -_3.pin5, -_3.pin6, -_3.pin7, -_3.pin8, LED.pin2
  N6: J1.pin1, A0_2.pin1
  N7: J1.pin12, TRIM.leg2
  N8: D7.Pin_1, D7.Pin_2, D6.Pin_1, D6.Pin_2, D5.Pin_1, D5.Pin_2
  N9: D7.Pin_3, D7.Pin_4, D6.Pin_3, D6.Pin_4, D5.Pin_3, D5.Pin_4, B1.pad, 10kΩ.Pin_1, B2.pad, B3.pad
  N10: TRIM.wiper, A0_2.pin2
  N11: 7905.GND, 5V.pin1, 5V.pin2, 5V.pin3, 5V.pin4, 5V.pin5, 5V.pin6, 5V.pin7, 5V.pin8
  N12: 10kΩ.Pin_0, LCD.pin1, -.pad, -_2.pad
  N13: LCD.pin2, 330Ω.Pin_0
  N14: LCD.pin3, +_2.pad
  N15: LCD.pin4, 10kΩ_5.Pin_0
  N16: LCD.pin5, 10kΩ_2.Pin_0
  N17: LCD.pin6, 10kΩ_3.Pin_0
  N18: LCD.pin7, 1kΩ.Pin_0
  N19: LCD.pin8, 10kΩ_4.Pin_0
  N20: RST.pad, 10kΩ_4.Pin_1
  N21: CE.pad, 1kΩ.Pin_1
  N22: DC.pad, 10kΩ_3.Pin_1
  N23: DIN.pad, 10kΩ_2.Pin_1
  N24: CLK.pad, 10kΩ_5.Pin_1
  N25: A0.pad, POT.pad
  N26: BL.pad, 330Ω.Pin_1
  N27: J2.pin8, D5_2.pin1
  N28: J2.pin9, D5_2.pin2
  N29: J2.pin10, D5_2.pin3
  N30: J2.pin11, LED.pin1

notes:
  USB SIDE
  Message Box
  Jeanette - v1.5
  RST
  VCC
  D1
  BL
  D2
  D3
  D4
  SERVO
  D6
  D7
  LCD
  BTN
  -
  D8
  GND

custom parts:
  NodeMCU V1.0: ESP8266 based NodeMCU
